// Logisim project 32bitALU.circ as structural Verilog: 1 circuit, main circuit main
module main (
  input  [31:0] Input_A,
  input  [31:0] Input_B,
  input  [31:0] DEFAULT_0,
  input  [3:0] SelOp,
  input  [4:0] in_5,
  input  [4:0] in_6,
  output [31:0] Output_C
);

  wire [31:0] _1_NOT_out, _4_AND_out, _5_OR_out, _6_XOR_out, adder_1_out, multiplier_1_out, shifter_1_out,
       shifter_2_out, subtractor_1_out;

  assign _1_NOT_out = ~Input_A;  // NOT_Gate _1_NOT, 32 bits wide
  Adder #(.width(32)) adder_1 (.a(Input_A), .b(Input_B), .out(adder_1_out));  // open: cin, cout
  Subtractor #(.width(32)) subtractor_1 (.a(Input_A), .b(Input_B), .out(subtractor_1_out));  // open: bin, bout
  Multiplier #(.width(32)) multiplier_1 (.a(Input_A), .b(Input_B), .out(multiplier_1_out));  // open: cin, cout
  assign _4_AND_out = Input_A & Input_B;  // AND_Gate _4_AND, 32 bits wide
  assign _5_OR_out = Input_A | Input_B;  // OR_Gate _5_OR, 32 bits wide
  assign _6_XOR_out = Input_A ^ Input_B;  // XOR_Gate _6_XOR, 32 bits wide
  Shifter #(.width(32), .shift("lr")) shifter_1 (.in(Input_A), .\dist (in_5), .out(shifter_1_out));
  Shifter #(.width(32)) shifter_2 (.in(Input_A), .\dist (in_6), .out(shifter_2_out));
  Multiplexer #(.select(4), .width(32)) multiplexer_1 (
    .in0(_1_NOT_out), .in1(adder_1_out), .in2(subtractor_1_out), .in3(multiplier_1_out), .in4(_4_AND_out),
    .in5(_5_OR_out), .in6(_6_XOR_out), .in7(shifter_1_out), .in8(shifter_2_out), .in9(DEFAULT_0),
    .in10(DEFAULT_0), .in11(DEFAULT_0), .in12(DEFAULT_0), .in13(DEFAULT_0), .in14(DEFAULT_0),
    .in15(DEFAULT_0), .out(Output_C), .sel(SelOp));  // open: en

  // Notes on the sheet:
  //   2-ADD
  //   3-SUB
  //   4-MUL
  //   7-RIGHT SHIFT
  //   8-LEFT SHIFT
endmodule
